# Fritzing sketch pin mapping raspberry pi 3b (saved by Fritzing 0.9.9b)

parts:
  Raspberry_Pi_1 = Raspberry Pi 3 [part_number=RPI-3-V1.2]
  DS1 = DS18B20 1-Wire Temperature Sensor [part_number=DS18B20]
  DS2 = DS18B20 1-Wire Temperature Sensor [part_number=DS18B20]
  R1 = Resistor [tolerance=±5% resistance=4.7k package="2010 [SMD]"]
  U1 = RELAY-SOLIDSTATE [package=relay-s108t02]

nets:
  VDD: Raspberry_Pi_1.3v3, DS1.VDD, DS2.VDD, R1.Pin_0
  N1: Raspberry_Pi_1.GPIO4, R1.Pin_1
  N2: Raspberry_Pi_1.GND, U1.-
  N3: Raspberry_Pi_1.GPIO17, U1.+
  GND: DS1.GND, DS2.GND
  N4: DS1.DQ, DS2.DQ
